// Logisim project 52200051-MaiNguyenPhuongTrang (1).circ as structural Verilog: 1 circuit, main circuit main
module main (
  input  in_1,
  input  in_2,
  input  in_3,
  input  in_4,
  output out_5,
  output out_6,
  output out_7,
  output out_8,
  output out_9,
  output out_10,
  output out_11,
  output out_12
);

  wire and_1_out, and_2_out, and_3_out, and_4_out, and_5_out, and_8_out, and_9_out, and_10_out, and_11_out,
       and_12_out, not_1_out, not_2_out, not_3_out, not_4_out, not_5_out, not_6_out, not_7_out, not_8_out,
       not_9_out, not_10_out, not_11_out, not_12_out, not_13_out, not_14_out, not_15_out, or_1_out, or_2_out,
       or_3_out;

  not not_1 (not_1_out, in_1);
  not not_2 (not_2_out, in_2);
  not not_3 (not_3_out, in_1);
  not not_4 (not_4_out, in_2);
  not not_5 (not_5_out, in_1);
  not not_6 (not_6_out, in_2);
  and and_1 (and_1_out, not_1_out, in_2);
  and and_2 (and_2_out, in_1, not_2_out);
  and and_3 (and_3_out, not_3_out, in_2);
  and and_4 (and_4_out, in_1, not_4_out);
  and and_5 (and_5_out, in_1, in_2);
  or or_1 (or_1_out, not_5_out, in_2);
  or or_2 (or_2_out, in_1, not_6_out);
  or or_3 (or_3_out, in_1, in_2);
  not not_7 (not_7_out, and_1_out);
  not not_8 (not_8_out, and_2_out);
  not not_9 (not_9_out, and_3_out);
  not not_10 (not_10_out, and_4_out);
  not not_11 (not_11_out, and_5_out);
  and and_6 (out_11, or_1_out, or_2_out, or_3_out);
  and and_7 (out_12, in_1, in_2);
  nand nand_1 (out_6, not_7_out, not_8_out);
  xor xor_1 (out_7, in_1, in_2);
  nand nand_2 (out_9, not_9_out, not_10_out, not_11_out);
  or or_4 (out_10, in_1, in_2);
  not not_12 (not_12_out, in_3);
  not not_13 (not_13_out, in_4);
  not not_14 (not_14_out, in_3);
  not not_15 (not_15_out, in_4);
  and and_8 (and_8_out, not_12_out, in_4);
  and and_9 (and_9_out, in_3, not_13_out);
  and and_10 (and_10_out, not_14_out, in_4);
  and and_11 (and_11_out, in_3, not_15_out);
  and and_12 (and_12_out, in_3, in_4);
  or or_5 (out_5, and_8_out, and_9_out);
  or or_6 (out_8, and_10_out, and_11_out, and_12_out);
endmodule
