// Logisim project 4-bit-adder.circ as structural Verilog: 2 circuits, main circuit main
module main (
  input  [3:0] in_1,
  input  [3:0] x,
  input  Cin,
  output Cout,
  output [3:0] S
);

  wire fa_2_out_5, fa_3_out_5, fa_4_out_5;

  FA fa_1 (.in_1(fa_2_out_5), .in_2(x[0]), .in_3(in_1[3]), .out_4(S[3]), .out_5(Cout));
  FA fa_2 (.in_1(fa_3_out_5), .in_2(x[1]), .in_3(in_1[2]), .out_4(S[2]), .out_5(fa_2_out_5));
  FA fa_3 (.in_1(fa_4_out_5), .in_2(x[2]), .in_3(in_1[1]), .out_4(S[1]), .out_5(fa_3_out_5));
  FA fa_4 (.in_1(Cin), .in_2(x[3]), .in_3(in_1[0]), .out_4(S[0]), .out_5(fa_4_out_5));

  // Notes on the sheet:
  //   y
endmodule

module FA (
  input  in_1,
  input  in_2,
  input  in_3,
  output out_4,
  output out_5
);

  wire and_1_out, and_2_out, xor_1_out;

  xor xor_1 (xor_1_out, in_1, in_2);
  and and_1 (and_1_out, in_2, in_1);
  xor xor_2 (out_4, xor_1_out, in_3);
  and and_2 (and_2_out, xor_1_out, in_3);
  or or_1 (out_5, and_1_out, and_2_out);
endmodule
