// Logisim project haftadder.circ as structural Verilog: 1 circuit, main circuit main
module main (
  input  in_1,
  input  b,
  output s,
  output out_4,
  output s_2,
  output c
);

  wire and_2_out, and_3_out, not_1_out, not_2_out;

  not not_1 (not_1_out, in_1);
  not not_2 (not_2_out, b);
  xor xor_1 (s, in_1, b);
  and and_1 (out_4, in_1, b);
  and and_2 (and_2_out, not_1_out, b);
  and and_3 (and_3_out, in_1, not_2_out);
  and and_4 (c, in_1, b);
  or or_1 (s_2, and_2_out, and_3_out);

  // Notes on the sheet:
  //   a
  //   haftadder
  //   A'B
  //   A.B'
  //   A.B
  //   c
  //   A'.B+AB'
endmodule
