// Logisim project xor_xnor.circ as structural Verilog: 1 circuit, main circuit main
module main (
  input  in_1,
  input  in_2,
  input  in_3,
  input  in_4,
  output out_5,
  output out_6,
  output out_7
);

  wire not_1_out, not_2_out, or_1_out, or_2_out;

  not not_1 (not_1_out, in_3);
  not not_2 (not_2_out, in_4);
  xor xor_1 (out_5, in_1, in_2);
  xnor xnor_1 (out_6, in_1, in_2);
  or or_1 (or_1_out, in_4, in_3);
  or or_2 (or_2_out, not_1_out, not_2_out);
  and and_1 (out_7, or_1_out, or_2_out);
endmodule
