// Logisim project 52200051_MaiNguyenPhuongTrang_manhsosanh.circ as structural Verilog: 1 circuit, main circuit main
module main (
  input  A,
  input  B,
  output A___B,
  output A___B_2,
  output A___B_3
);

  wire and_2_out, and_3_out, not_1_out, not_2_out, not_3_out, not_4_out;

  not not_1 (not_1_out, A);
  not not_2 (not_2_out, A);
  not not_3 (not_3_out, B);
  not not_4 (not_4_out, B);
  and and_1 (A___B, not_1_out, B);
  and and_2 (and_2_out, not_2_out, not_3_out);
  and and_3 (and_3_out, A, B);
  and and_4 (A___B_3, A, not_4_out);
  or or_1 (A___B_2, and_2_out, and_3_out);

  // Notes on the sheet:
  //   A'
  //   B
  //   A'
  //   B'
  //   A
  //   B
  //   A
  //   B'
  //   A'.B
  //   A'.B'
  //   AB
  //   A.B'
  //   A'.B' + A.B
endmodule
