// Logisim project DENLED.circ as structural Verilog: 5 circuits, main circuit main
module main (
  input  X,
  input  in_2,
  input  in_3,
  input  Y,
  input  in_5,
  input  in_6,
  input  X_2,
  input  Y_2,
  input  Z,
  input  X_3,
  input  Y_3
);

  wire full_adder_1_c, full_adder_1_s, half_adder_1_c, half_adder_1_s, led_1_d0, led_1_d1, led_1_d2,
       led_1_d3, led_1_d4, led_1_d5, led_1_d6, sr_ff_1_q, sr_ff_1_q_prime;

  LED led_1 (
    .a(in_2), .b(in_3), .c(in_5), .d(in_6), .D0(led_1_d0), .D1(led_1_d1), .D2(led_1_d2), .D3(led_1_d3),
    .D4(led_1_d4), .D5(led_1_d5), .D6(led_1_d6));
  _7_Segment_Display u_7_segment_display_1 (
    .g(led_1_d0), .f(led_1_d1), .a(led_1_d2), .b(led_1_d3), .e(led_1_d4), .d(led_1_d5), .c(led_1_d6));  // open: dp
  half_adder half_adder_1 (.x(X), .y(Y), .c(half_adder_1_c), .s(half_adder_1_s));
  SR_Flip_Flop sr_ff_1 (.S(X_3), .R(Y_3), .Q_prime(sr_ff_1_q_prime), .Q(sr_ff_1_q));
  LED_part led_2 (.in(half_adder_1_c));
  LED_part led_3 (.in(half_adder_1_s));
  full_adder full_adder_1 (.x(X_2), .y(Y_2), .z(Z), .c(full_adder_1_c), .s(full_adder_1_s));
  LED_part led_4 (.in(sr_ff_1_q_prime));
  LED_part led_5 (.in(sr_ff_1_q));
  LED_part led_6 (.in(full_adder_1_c));
  LED_part led_7 (.in(full_adder_1_s));

  // Notes on the sheet:
  //   HALD ADDER
  //   FULL ADDER
  //   SR FLIP-FLOP
  //   LED
  //   LED
  //   LED
  //   LED
  //   LED
  //   LED
endmodule

module half_adder (
  input  x,
  input  y,
  output c,
  output s
);

  wire and_2_out, and_3_out, not_1_out, not_2_out;

  not not_1 (not_1_out, y);
  not not_2 (not_2_out, x);
  and and_1 (c, x, y);
  and and_2 (and_2_out, x, not_1_out);
  and and_3 (and_3_out, not_2_out, y);
  or or_1 (s, and_2_out, and_3_out);
endmodule

module full_adder (
  input  x,
  input  y,
  input  z,
  output c,
  output s
);

  wire and_1_out, and_2_out, and_3_out, and_4_out, and_5_out, and_6_out, and_7_out, not_1_out, not_2_out,
       not_3_out, not_4_out, not_5_out, not_6_out;

  and and_1 (and_1_out, y, z);
  and and_2 (and_2_out, x, z);
  and and_3 (and_3_out, x, y);
  and and_4 (and_4_out, x, y, z);
  not not_1 (not_1_out, x);
  not not_2 (not_2_out, y);
  not not_3 (not_3_out, x);
  not not_4 (not_4_out, z);
  not not_5 (not_5_out, y);
  not not_6 (not_6_out, z);
  or or_1 (c, and_1_out, and_2_out, and_3_out);
  and and_5 (and_5_out, not_1_out, not_2_out, z);
  and and_6 (and_6_out, not_3_out, y, not_4_out);
  and and_7 (and_7_out, x, not_5_out, not_6_out);
  or or_2 (s, and_5_out, and_6_out, and_7_out, and_4_out);
endmodule

module SR_Flip_Flop (
  input  S,
  input  R,
  output Q_prime,
  output Q
);

  nor nor_1 (Q_prime, S, Q);
  nor nor_2 (Q, Q_prime, R);
endmodule

module LED (
  input  a,
  input  b,
  input  c,
  input  d,
  output D0,
  output D1,
  output D2,
  output D3,
  output D4,
  output D5,
  output D6
);

  wire and_1_out, and_2_out, and_3_out, and_4_out, and_5_out, and_6_out, and_7_out, and_8_out, and_9_out,
       and_10_out, and_11_out, and_12_out, and_13_out, and_14_out, and_15_out, and_16_out, and_17_out,
       and_18_out, and_19_out, and_20_out, and_21_out, and_22_out, and_23_out, and_24_out, and_25_out,
       and_26_out, and_27_out, and_28_out, not_1_out, not_2_out, not_3_out, not_4_out, not_5_out, not_6_out,
       not_7_out, not_8_out, not_9_out, not_10_out, not_11_out, not_12_out, not_13_out, not_14_out,
       not_15_out, not_16_out, not_17_out, not_18_out, not_19_out, not_20_out, not_21_out, not_22_out,
       not_23_out, not_24_out, not_25_out, not_26_out, not_27_out, not_28_out, not_29_out, not_30_out,
       not_31_out, not_32_out, not_33_out, not_34_out, not_35_out, not_36_out, not_37_out, not_38_out;

  not not_1 (not_1_out, a);
  not not_2 (not_2_out, b);
  not not_3 (not_3_out, a);
  not not_4 (not_4_out, c);
  not not_5 (not_5_out, d);
  not not_6 (not_6_out, b);
  not not_7 (not_7_out, c);
  not not_8 (not_8_out, c);
  and and_1 (and_1_out, not_8_out, not_9_out);
  not not_9 (not_9_out, d);
  and and_2 (and_2_out, b, not_10_out);
  not not_10 (not_10_out, c);
  and and_3 (and_3_out, b, not_11_out);
  not not_11 (not_11_out, d);
  not not_12 (not_12_out, d);
  not not_13 (not_13_out, a);
  and and_4 (and_4_out, not_13_out, c);
  and and_5 (and_5_out, a, not_14_out);
  not not_14 (not_14_out, c);
  not not_15 (not_15_out, a);
  and and_6 (and_6_out, not_15_out, not_16_out, not_17_out);
  not not_16 (not_16_out, c);
  not not_17 (not_17_out, d);
  not not_18 (not_18_out, b);
  and and_7 (and_7_out, not_18_out, not_19_out);
  not not_19 (not_19_out, c);
  not not_20 (not_20_out, b);
  and and_8 (and_8_out, not_20_out, not_21_out);
  not not_21 (not_21_out, d);
  not not_22 (not_22_out, a);
  and and_9 (and_9_out, not_22_out, c, d);
  not not_23 (not_23_out, b);
  and and_10 (and_10_out, not_23_out, not_24_out);
  not not_24 (not_24_out, d);
  and and_11 (and_11_out, c, not_25_out);
  not not_25 (not_25_out, d);
  and and_12 (and_12_out, a, c);
  and and_13 (and_13_out, a, b);
  not not_26 (not_26_out, a);
  not not_27 (not_27_out, b);
  and and_14 (and_14_out, not_26_out, not_27_out, not_28_out);
  not not_28 (not_28_out, d);
  not not_29 (not_29_out, b);
  and and_15 (and_15_out, not_29_out, c, d);
  and and_16 (and_16_out, b, not_30_out, d);
  not not_30 (not_30_out, c);
  and and_17 (and_17_out, b, c, not_31_out);
  not not_31 (not_31_out, d);
  and and_18 (and_18_out, a, not_32_out);
  not not_32 (not_32_out, c);
  not not_33 (not_33_out, a);
  and and_19 (and_19_out, not_33_out, not_34_out);
  not not_34 (not_34_out, c);
  not not_35 (not_35_out, a);
  and and_20 (and_20_out, not_35_out, d);
  not not_36 (not_36_out, c);
  and and_21 (and_21_out, not_36_out, d);
  not not_37 (not_37_out, a);
  and and_22 (and_22_out, not_37_out, b);
  and and_23 (and_23_out, a, not_38_out);
  not not_38 (not_38_out, b);
  and and_24 (and_24_out, not_1_out, not_2_out, c);
  and and_25 (and_25_out, not_3_out, b, not_4_out, d);
  and and_26 (and_26_out, b, c, not_5_out);
  and and_27 (and_27_out, a, not_6_out, not_7_out);
  and and_28 (and_28_out, a, c, d);
  or or_1 (D1, and_1_out, and_2_out, and_3_out, a);
  or or_2 (D2, not_12_out, and_4_out, b, and_5_out);
  or or_3 (D3, and_6_out, and_7_out, and_8_out, and_9_out);
  or or_4 (D4, and_10_out, and_11_out, and_12_out, and_13_out);
  or or_5 (D5, and_14_out, and_15_out, and_16_out, and_17_out, and_18_out);
  or or_6 (D6, and_19_out, and_20_out, and_21_out, and_22_out, and_23_out);
  or or_7 (D0, and_24_out, and_25_out, and_26_out, and_27_out, and_28_out);
endmodule
