// Logisim project baitaptuan3.circ as structural Verilog: 6 circuits, main circuit main
module main (
  input  A,
  input  B,
  output X,
  output Y
);

  wire and_1_out, and_2_out, not_1_out, not_2_out, not_3_out;

  not not_1 (not_1_out, B);
  not not_2 (not_2_out, A);
  not not_3 (not_3_out, B);
  or or_1 (X, not_1_out, A);
  and and_1 (and_1_out, not_2_out, B);
  and and_2 (and_2_out, A, not_3_out);
  or or_2 (Y, and_1_out, and_2_out);

  // Notes on the sheet:
  //   CAU 3
endmodule

module LAB2_2 (
  input  A,
  input  B,
  output S,
  output C
);

  xor xor_1 (S, A, B);
  and and_1 (C, A, B);
endmodule

module CAU1 (
  input  in_1,
  input  in_2,
  input  in_3,
  input  in_4,
  input  [3:0] in_5
);

  LED led_1 (.in(in_5[3]));
  Hex_Digit_Display hex_digit_display_1 (.value({in_4, in_3, in_2, in_1}));  // open: dp
  LED led_2 (.in(in_5[0]));
  LED led_3 (.in(in_5[1]));
  LED led_4 (.in(in_5[2]));
  Hex_Digit_Display hex_digit_display_2 (.value(in_5));  // open: dp
endmodule

module CAU2 (
  input  A,
  input  A_2
);

  wire lab2_2_1_c, lab2_2_1_s;

  LAB2_2 lab2_2_1 (.A(A), .B(A_2), .S(lab2_2_1_s), .C(lab2_2_1_c));
  LED S (.in(lab2_2_1_s));
  LED C (.in(lab2_2_1_c));

  // Notes on the sheet:
  //   CAU2
endmodule

module CAU4 (
  input  in_1
);

  Clock clock_1 (.out(in_1));
  LED led_1 (.in(in_1));
  LED led_2 (.in(in_1));
  LED led_3 (.in(in_1));
endmodule

module CAU5 (
);

  wire clock_1_out;
  wire [2:0] register_1_q, rom_1_data;

  Clock clock_1 (.out(clock_1_out));
  Register #(.width(3)) register_1 (.en(clock_1_out), .Q(register_1_q), .clk(clock_1_out));  // open: D, clr
  ROM #(.addrWidth(3), .dataWidth(3)) rom_1 (.addr(register_1_q), .data(rom_1_data));  // open: sel
  LED led_1 (.in(rom_1_data[2]));
  LED led_2 (.in(rom_1_data[1]));
  LED led_3 (.in(rom_1_data[0]));

  // Notes on the sheet:
  //   clock
  //   Traffic Led
  //   đèn đỏ
  //   đèn vàng
  //   đèn xanh
endmodule
