// Logisim project 52200051_MaiNguyenPhuongTrang.circ as structural Verilog: 3 circuits, main circuit main
module main (
);

  wire clock_1_out;
  wire [3:0] counter_1_q, rom_1_data;

  Clock clock_1 (.out(clock_1_out));
  Counter #(.width(4), .max('hf)) counter_1 (
    .count(clock_1_out), .Q(counter_1_q), .clk(clock_1_out));  // open: load, D, carry, clr
  ROM #(.addrWidth(4), .dataWidth(4)) rom_1 (.addr(counter_1_q), .data(rom_1_data));  // open: sel
  Hex_Digit_Display hex_digit_display_1 (.value(rom_1_data));  // open: dp

  // Notes on the sheet:
  //   CLOCK
  //   COUNTER
  //   ROM
  //   contents of rom_1 (hex, n*v repeats v):
  //   0 1 2 3 4 5 6 7 8 9 a b c d e f
  //   HEXA DIGITAL DISPLAY
endmodule

module TRAFFICLIGHT (
);

  wire clock_1_out;
  wire [2:0] counter_1_q, rom_1_data;

  Clock clock_1 (.out(clock_1_out));
  Counter #(.width(3), .max('h7)) counter_1 (
    .count(clock_1_out), .Q(counter_1_q), .clk(clock_1_out));  // open: load, D, carry, clr
  ROM #(.addrWidth(3), .dataWidth(3)) rom_1 (.addr(counter_1_q), .data(rom_1_data));  // open: sel
  LED led_1 (.in(rom_1_data[2]));
  LED led_2 (.in(rom_1_data[1]));
  LED led_3 (.in(rom_1_data[0]));

  // Notes on the sheet:
  //   CLOCK
  //   COUNTER
  //   ROM
  //   contents of rom_1 (hex, n*v repeats v):
  //   1 1 2 2 4 4 1 1
  //   RED
  //   YELLOW
  //   GREEN
endmodule

module KITU (
);

  wire button_1_out, clock_1_out;
  wire [5:0] counter_1_q;
  wire [6:0] rom_1_data;

  Clock clock_1 (.out(clock_1_out));
  Counter #(.width(6), .max('h3f)) counter_1 (
    .Q(counter_1_q), .clk(clock_1_out), .clr(button_1_out));  // open: load, D, count, carry
  Button button_1 (.out(button_1_out));
  ROM #(.addrWidth(6), .dataWidth(7)) rom_1 (.addr(counter_1_q), .data(rom_1_data));  // open: sel
  TTY tty_1 (.data(rom_1_data), .clk(clock_1_out), .clr(button_1_out));  // open: we

  // Notes on the sheet:
  //   contents of rom_1 (hex, n*v repeats v):
  //   58 69 6e 20 63 68 61 6f 20 63 61 63 20 62 61 6e 21 20 43 68 75 63 20 63 61 63 20 62 61 6e 20 68 6f
  //   63 20 74 6f 74
endmodule
